# Fritzing sketch Chris_Stefan_Roboter_Platine (saved by Fritzing 0.9.3b)
perfboards: 1

parts:
  IC1 = L293D [package=THT]
  L1 = Solenoid
  L2 = Solenoid
  VCC1 = Battery
  J1 = female pin header, 3 pins [form="♀ (female)"]
  J2 = female pin header, 3 pins [form="♀ (female)"]

nets:
  N1: IC1.In_1, J2.pin1
  N2: IC1.Out_1_(_Controlled_by_Enable_1_), L2.pin2
  N3: IC1.0V, VCC1.-, J2.pin3
  N4: IC1.Out_2_(_Controlled_by_Enable_1_), L2.pin1
  N5: IC1.In_2, J2.pin2
  N6: IC1.+Vmotor, VCC1.+
  N7: IC1.In_3, J1.pin2
  N8: IC1.Out_3_(_Controlled_by_Enable_2_), L1.pin1
  N9: IC1.Out_4_(_Controlled_by_Enable_2_), L1.pin2
  N10: IC1.In_4, J1.pin3
  N11: IC1.+V, J1.pin1

notes:
  MotorPlatine
  Schwarze Leitungen können bilden die Lochgrenze
  Grau sind Drahtbrücken unter der Platine
  Weiß Drahtbrücken auf der Platine
  Motor Links
  Motor Rechts
